# Fritzing sketch circuit (saved by Fritzing 0.9.3b)

parts:
  Part2 = Arduino Uno (Rev3)
  Part3 = Arduino Uno (Rev3)
  S1 = H-Bridge with L298N
  U1 = LM2596 step down module
  BATT1 = LiPoly Battery (1300mAh)
  F1 = FUSE [package=fuse_5mm]
  S2 = Round Pushbutton
  M1 = ESC
  920KV_Motor1 = DJI 920 KV Motor
  M2 = DC Motor
  Transceiver1 = nRF24L01 [package=module]
  Transceiver2 = nRF24L01 [package=module]
  LED1 = RGB LED - (4 legs) [package="5 mm [THT]"]
  Part4 = Thumb Joystick
  R1 = Resistor [tolerance=±5% resistance=220 package="0603 [SMD]"]
  R2 = Resistor [tolerance=±5% resistance=220 package="0603 [SMD]"]
  R3 = Resistor [tolerance=±5% resistance=220 package="0603 [SMD]"]
  U2 = SWITCH-SPST-2 [package=r_sw_th]
  BAT1 = BC9VPC [package=bc9vpc]
  LED2 = RGB LED - (4 legs) [package="5 mm [THT]"]
  R4 = Resistor [tolerance=±5% resistance=220 package="0603 [SMD]"]
  R6 = Resistor [tolerance=±5% resistance=220 package="0603 [SMD]"]
  R7 = Resistor [tolerance=±5% resistance=220 package="0603 [SMD]"]

nets:
  N1: Part2.D9_PWM, M1.DATA
  N2: Part2.D11_PWM/MOSI, S1.IN2
  N3: Part2.D12/MISO, S1.IN1
  N4: Part2.D13/SCK, S1.ENA
  GND: Part2.GND, S1.GND, U1.IN-, U1.OUT-, BATT1.negative, Transceiver1.GND
  N5: Part2.D2, Transceiver1.CSN
  N6: Part2.D3_PWM, Transceiver1.MOSI
  N7: Part2.D5_PWM, Transceiver1.MISO
  N8: Part2.D6_PWM, Transceiver1.SCK
  N9: Part2.D7, Transceiver1.CE
  5V: Part2.5V, Transceiver1.VCC
  N10: Part2.VIN, U1.OUT+
  N11: Part3.A1, Part4.VERT
  N12: Part3.A2, Part4.HORZ
  N13: Part3.D8, R7.Pin_0
  N14: Part3.D9_PWM, R6.Pin_0
  N15: Part3.D10_PWM/SS, R4.Pin_0
  N16: Part3.D11_PWM/MOSI, R3.Pin_0
  N17: Part3.D12/MISO, R1.Pin_0
  N18: Part3.D13/SCK, R2.Pin_0
  GND_2: Part3.GND, Transceiver2.GND, LED1.common_anode, Part4.GND, BAT1.V-, LED2.common_anode
  N19: Part3.D1/TX, Transceiver2.CSN
  N20: Part3.D2, Transceiver2.MOSI
  N21: Part3.D4, Transceiver2.MISO
  N22: Part3.D5_PWM, Transceiver2.SCK
  N23: Part3.D6_PWM, Transceiver2.CE
  VCC: Part3.5V, Transceiver2.VCC, Part4.VCC
  N24: Part3.VIN, U2.O
  N25: S1.12V, U1.IN+, F1.2
  N26: S1.M1-01, M2.pin_2
  N27: S1.M1-02, M2.pin_1
  N28: BATT1.positive, S2.leg0
  N29: F1.1, S2.leg1
  N30: M1.U, 920KV_Motor1.u
  N31: M1.V, 920KV_Motor1.v
  N32: M1.W, 920KV_Motor1.w
  N33: LED1.red_cathode, R2.Pin_1
  N34: LED1.green_cathode, R1.Pin_1
  N35: LED1.blue_cathode, R3.Pin_1
  N36: U2.P, BAT1.V+
  N37: LED2.red_cathode, R4.Pin_1
  N38: LED2.green_cathode, R6.Pin_1
  N39: LED2.blue_cathode, R7.Pin_1

custom parts:
  H-Bridge with L298N: h-bridge
  LM2596 step down module: LM2596 DC-DC step down power supply module 3 A.
  LiPoly Battery (1300mAh): Lithium Ion Polymer Battery (1300mAh)
  DJI 920 KV Motor: DJI Brushless Outrunner 2212/920K Motor F330-550
  nRF24L01: nRF24L01 module
